// Logisim project addonsNew.circ as structural Verilog: 7 circuits, main circuit REG32_LD
module REG32_LD (
  input  [31:0] I15__0,
  input  LD,
  input  mr,
  input  CLK,
  output [31:0] A15__0
);

  // REG16_LD reg16_ld_1: pin names not known; wires that end beside it: CLK, mr, I15__0[31:16], A15__0[31:16], LD
  // REG16_LD reg16_ld_2: pin names not known; wires that end beside it: CLK, mr, I15__0[15:0], A15__0[15:0], LD

  // Notes on the sheet:
  //   __
endmodule

module KMADR (
  input  immed,
  input  memdir,
  input  regdir,
  input  regindpom,
  output [3:0] Adr3__0
);

  assign Adr3__0 = immed ? 4'b0010 : 4'bz;  // Controlled_Buffer controlled_buffer_1
  assign Adr3__0 = memdir ? 4'b0100 : 4'bz;  // Controlled_Buffer controlled_buffer_2
  assign Adr3__0 = regdir ? 4'b0101 : 4'bz;  // Controlled_Buffer controlled_buffer_3
  assign Adr3__0 = regindpom ? 4'b0111 : 4'bz;  // Controlled_Buffer controlled_buffer_4
endmodule

module KMOPR (
  input  LD,
  input  ST,
  input  ADD,
  input  SUB,
  input  BLSS,
  input  JLEQ,
  input  JMP,
  input  JSR,
  input  RTS,
  input  RTI,
  input  HALT,
  output [5:0] Adr5__0
);

  assign Adr5__0 = LD ? 6'b000010 : 6'bz;  // Controlled_Buffer controlled_buffer_1
  assign Adr5__0 = ST ? 6'b000100 : 6'bz;  // Controlled_Buffer controlled_buffer_2
  assign Adr5__0 = ADD ? 6'b001010 : 6'bz;  // Controlled_Buffer controlled_buffer_3
  assign Adr5__0 = SUB ? 6'b001100 : 6'bz;  // Controlled_Buffer controlled_buffer_4
  assign Adr5__0 = BLSS ? 6'b001110 : 6'bz;  // Controlled_Buffer controlled_buffer_5
  assign Adr5__0 = JLEQ ? 6'b010000 : 6'bz;  // Controlled_Buffer controlled_buffer_6
  assign Adr5__0 = JMP ? 6'b010001 : 6'bz;  // Controlled_Buffer controlled_buffer_7
  assign Adr5__0 = JSR ? 6'b010010 : 6'bz;  // Controlled_Buffer controlled_buffer_8
  assign Adr5__0 = RTS ? 6'b010111 : 6'bz;  // Controlled_Buffer controlled_buffer_9
  assign Adr5__0 = RTI ? 6'b011110 : 6'bz;  // Controlled_Buffer controlled_buffer_10
  assign Adr5__0 = HALT ? 6'b100010 : 6'bz;  // Controlled_Buffer controlled_buffer_11
endmodule

module REG6_INC_LD (
  input  [5:0] I5__0,
  input  LD,
  input  INC,
  input  mr,
  input  CLK,
  output [5:0] A5__0
);

  wire reg2m_inc_ld_1_p7, reg2m_inc_ld_2_p8;

  // REG2m_INC_LD reg2m_inc_ld_1: pin names not known; wires that end beside it: CLK, mr, I5__0[5:4], A5__0[5:4], LD, INC, reg2m_inc_ld_1_p7
  // REG2m_INC_LD reg2m_inc_ld_2: pin names not known; wires that end beside it: CLK, reg2m_inc_ld_1_p7, mr, I5__0[3:2], A5__0[3:2], LD, INC, reg2m_inc_ld_2_p8
  // REG2m_INC_LD reg2m_inc_ld_3: pin names not known; wires that end beside it: CLK, reg2m_inc_ld_2_p8, mr, I5__0[1:0], A5__0[1:0], LD, INC, INC

  // Notes on the sheet:
  //   __
endmodule

module KADDRMX (
  input  immed,
  input  regdir,
  input  memdir,
  input  memind,
  input  preinc,
  input  postinc,
  input  regindpom,
  output [4:0] Adr4__0
);

  assign Adr4__0 = immed ? 5'b00010 : 5'bz;  // Controlled_Buffer controlled_buffer_1
  assign Adr4__0 = regdir ? 5'b00011 : 5'bz;  // Controlled_Buffer controlled_buffer_2
  assign Adr4__0 = memdir ? 5'b00101 : 5'bz;  // Controlled_Buffer controlled_buffer_3
  assign Adr4__0 = memind ? 5'b00110 : 5'bz;  // Controlled_Buffer controlled_buffer_4
  assign Adr4__0 = preinc ? 5'b01100 : 5'bz;  // Controlled_Buffer controlled_buffer_5
  assign Adr4__0 = postinc ? 5'b10000 : 5'bz;  // Controlled_Buffer controlled_buffer_6
  assign Adr4__0 = regindpom ? 5'b10100 : 5'bz;  // Controlled_Buffer controlled_buffer_7
endmodule

module KEXECMX (
  input  HALT,
  input  PUSH,
  input  LD,
  input  RTI_POPPSW,
  input  RTS,
  input  POP,
  input  skok2,
  input  JLEQ,
  input  JSR,
  input  JMP,
  input  TST,
  input  ASL,
  input  XOR,
  input  JADR,
  input  STRLEN,
  input  STORE,
  output [5:0] Adr4__0
);

  assign Adr4__0 = HALT ? 6'b000010 : 6'bz;  // Controlled_Buffer controlled_buffer_1
  assign Adr4__0 = PUSH ? 6'b000011 : 6'bz;  // Controlled_Buffer controlled_buffer_2
  assign Adr4__0 = LD ? 6'b001001 : 6'bz;  // Controlled_Buffer controlled_buffer_3
  assign Adr4__0 = RTI_POPPSW ? 6'b001011 : 6'bz;  // Controlled_Buffer controlled_buffer_4
  assign Adr4__0 = RTS ? 6'b010000 : 6'bz;  // Controlled_Buffer controlled_buffer_5
  assign Adr4__0 = POP ? 6'b010101 : 6'bz;  // Controlled_Buffer controlled_buffer_6
  assign Adr4__0 = skok2 ? 6'b011100 : 6'bz;  // Controlled_Buffer controlled_buffer_7
  assign Adr4__0 = JLEQ ? 6'b011110 : 6'bz;  // Controlled_Buffer controlled_buffer_8
  assign Adr4__0 = JMP ? 6'b100101 : 6'bz;  // Controlled_Buffer controlled_buffer_9
  assign Adr4__0 = JSR ? 6'b100100 : 6'bz;  // Controlled_Buffer controlled_buffer_10
  assign Adr4__0 = TST ? 6'b100110 : 6'bz;  // Controlled_Buffer controlled_buffer_11
  assign Adr4__0 = ASL ? 6'b101000 : 6'bz;  // Controlled_Buffer controlled_buffer_12
  assign Adr4__0 = XOR ? 6'b101010 : 6'bz;  // Controlled_Buffer controlled_buffer_13
  assign Adr4__0 = JADR ? 6'b101011 : 6'bz;  // Controlled_Buffer controlled_buffer_14
  assign Adr4__0 = STRLEN ? 6'b101100 : 6'bz;  // Controlled_Buffer controlled_buffer_15
  assign Adr4__0 = STORE ? 6'b110011 : 6'bz;  // Controlled_Buffer controlled_buffer_16
endmodule

module _50MEM (
  input  [5:0] in_1,
  input  in_2,
  input  [15:0] in_3,
  input  [31:0] in_4
);

  ROM #(.addrWidth(6), .dataWidth(16)) rom_1 (.addr(in_1), .data(in_3), .sel(in_2));
  ROM #(.addrWidth(6), .dataWidth(32)) rom_2 (.addr(in_1), .data(in_4), .sel(in_2));
endmodule
