// Logisim project main.circ as structural Verilog: 8 circuits, main circuit COMPUTER
module COMPUTER (
);

  wire BTN_RST_out, CLK, cpu_1_inta, interrupt_interface_8_1_p4, interrupt_interface_8_1_p5,
       interrupt_interface_8_1_p6, interrupt_interface_8_1_p7, interrupt_interface_8_1_p8,
       interrupt_interface_8_1_p9, interrupt_interface_8_1_p10, interrupt_interface_8_1_p11,
       pull_resistor_4_node, pull_resistor_5_node, ram_1_out_8, rst;
  wire [2:0] cpu_1_uext1__0;
  wire [7:0] interrupt_interface_8_1_p1, pull_resistor_1_node, ram_1_out_7;
  wire [15:0] pull_resistor_3_node;

  Button BTN_RST (.out(BTN_RST_out));
  Clock u_CLK (.out(CLK));
  // RisingEdge risingedge_1: pin names not known; wires that end beside it: BTN_RST_out, CLK, rst
  RAM ram_1 (
    .in_1(pull_resistor_3_node), .in_2(CLK), .in_3(pull_resistor_1_node), .in_4(pull_resistor_4_node),
    .in_5(pull_resistor_5_node), .in_6(rst), .out_7(ram_1_out_7), .out_8(ram_1_out_8));
  Pull_Resistor pull_resistor_1 (.node(pull_resistor_1_node));
  Pull_Resistor pull_resistor_2 (.node(ram_1_out_7));
  Pull_Resistor pull_resistor_3 (.node(pull_resistor_3_node));
  Pull_Resistor pull_resistor_4 (.node(pull_resistor_4_node));
  Pull_Resistor pull_resistor_5 (.node(pull_resistor_5_node));
  Pull_Resistor pull_resistor_6 (.node(ram_1_out_8));
  CPU cpu_1 (
    .in_1(rst), .in_2(CLK), .in_3(ram_1_out_8), .in_4(ram_1_out_7), .ABUS(pull_resistor_3_node),
    .DOUTBUS(pull_resistor_1_node), .out_8(pull_resistor_4_node), .out_9(pull_resistor_5_node),
    .inta(cpu_1_inta), .intr3__0(interrupt_interface_8_1_p1), .UEXT1__0(cpu_1_uext1__0));
  // INTERRUPT_INTERFACE_8 interrupt_interface_8_1: pin names not known; wires that end beside it: interrupt_interface_8_1_p1, cpu_1_inta, cpu_1_uext1__0, interrupt_interface_8_1_p4, interrupt_interface_8_1_p5, interrupt_interface_8_1_p6, interrupt_interface_8_1_p7, interrupt_interface_8_1_p8, interrupt_interface_8_1_p9, interrupt_interface_8_1_p10, interrupt_interface_8_1_p11, CLK
  Button BTN_INTR7 (.out(interrupt_interface_8_1_p4));
  Button BTN_INTR6 (.out(interrupt_interface_8_1_p5));
  Button BTN_INTR5 (.out(interrupt_interface_8_1_p6));
  Button BTN_INTR4 (.out(interrupt_interface_8_1_p7));
  Button BTN_INTR3 (.out(interrupt_interface_8_1_p8));
  Button BTN_INTR2 (.out(interrupt_interface_8_1_p9));
  Button BTN_INTR1 (.out(interrupt_interface_8_1_p10));
  Button BTN_INTR0 (.out(interrupt_interface_8_1_p11));
endmodule

module CPU (
  input  in_1,
  input  in_2,
  input  in_3,
  input  [7:0] in_4,
  input  [7:0] intr3__0,
  output [15:0] ABUS,
  output [7:0] DOUTBUS,
  output out_8,
  output out_9,
  output inta,
  output [2:0] UEXT1__0
);

  wire common_1_out_35;
  wire [3:0] common_1_addrbus, common_1_phaseffbus;
  wire [6:0] common_1_out_34, pull_resistor_2_node;
  wire [7:0] pull_resistor_6_node;
  wire [8:0] pull_resistor_4_node;
  wire [10:0] common_1_instrucbus;
  wire [15:0] A, ALU, B, INTRADDR, PSW;
  wire [19:0] common_1_out_29;
  wire [25:0] pull_resistor_7_node;

  COMMON common_1 (
    .CLK(in_2), .RST(in_1), .DIN(in_4), .CMEMBUS(pull_resistor_7_node), .MAR(ABUS), .MDR(DOUTBUS),
    .PHASEFFBUS(common_1_phaseffbus), .INSTRUCBUS(common_1_instrucbus), .ADDRBUS(common_1_addrbus),
    .PSW(PSW), .CREGBUS(pull_resistor_4_node), .CFFBUS(pull_resistor_6_node), .B(B), .A(A),
    .CPSW(pull_resistor_2_node), .ALU(ALU), .IVTPPDSP(INTRADDR), .out_29(common_1_out_29),
    .out_34(common_1_out_34), .out_35(common_1_out_35));  // open: out_24, out_27, out_26, out_16, in_8, out_23, out_20, out_19, out_21, out_17, out_32, out_33, out_15, out_31, out_30
  Pull_Resistor pull_resistor_1 (.node(common_1_instrucbus));
  Pull_Resistor pull_resistor_2 (.node(pull_resistor_2_node));
  Pull_Resistor pull_resistor_3 (.node(common_1_phaseffbus));
  Pull_Resistor pull_resistor_4 (.node(pull_resistor_4_node));
  Pull_Resistor pull_resistor_5 (.node(common_1_addrbus));
  Pull_Resistor pull_resistor_6 (.node(pull_resistor_6_node));
  Pull_Resistor pull_resistor_7 (.node(pull_resistor_7_node));
  Pull_Resistor pull_resistor_8 (.node(common_1_out_29));
  Pull_Resistor pull_resistor_9 (.node(common_1_out_35));
  Pull_Resistor pull_resistor_10 (.node(common_1_out_34));
  FETCH fetch_1 (
    .in_1(in_1), .in_2(in_2), .in_3(in_3), .PHASEFFBUS(common_1_phaseffbus),
    .INSTRUCBUS(common_1_instrucbus), .ADDRBUS(common_1_addrbus), .PSW(PSW), .rdMEM(out_9),
    .CMEMBUS(pull_resistor_7_node), .CFFBUS(pull_resistor_6_node), .CREGBUS(pull_resistor_4_node),
    .in_8(common_1_out_29), .in_9(common_1_out_34));  // open: out_12, out_14
  ADDR addr_1 (
    .in_1(in_1), .in_2(in_2), .in_3(in_3), .PHASEFFBUS(common_1_phaseffbus),
    .INSTRUCBUS(common_1_instrucbus), .ADDRBUS(common_1_addrbus), .rdMEM(out_9),
    .CMEMBUS(pull_resistor_7_node), .CFFBUS(pull_resistor_6_node), .CREGBUS(pull_resistor_4_node),
    .in_7(common_1_out_29), .in_8(common_1_out_34));  // open: out_11
  EXEC exec_1 (
    .in_1(in_1), .in_2(in_2), .in_3(in_3), .B(B), .PHASEFFBUS(common_1_phaseffbus),
    .INSTRUCBUS(common_1_instrucbus), .ADDRBUS(common_1_addrbus), .PSW(PSW), .A(A), .ALU(ALU),
    .CMEMBUS(pull_resistor_7_node), .CFFBUS(pull_resistor_6_node), .CREGBUS(pull_resistor_4_node),
    .CPSW(pull_resistor_2_node), .rdMEM(out_9), .wrMEM(out_8), .in_9(common_1_out_29),
    .in_10(common_1_out_34), .in_11(common_1_out_35));  // open: out_16, out_15
  INTR intr_1 (
    .in_1(in_1), .in_2(in_2), .in_3(in_3), .PHASEFFBUS(common_1_phaseffbus),
    .INSTRUCBUS(common_1_instrucbus), .PSW(PSW), .intr(intr3__0), .ADDIVTP(INTRADDR),
    .CMEMBUS(pull_resistor_7_node), .CFFBUS(pull_resistor_6_node), .CREGBUS(pull_resistor_4_node),
    .rdMEM(out_9), .wrMEM(out_8), .UEXT1__0(UEXT1__0), .inta(inta));  // open: out_13, out_15, out_12

  // Other names for the same wires on the sheet: CLK = in_2; DIN7__0[7:0] = in_4; FCBUS = in_3;
  //   intr7__0[7:0] = intr3__0; MAR[15:0] = ABUS; MDR[7:0] = DOUTBUS; RD = out_9; rst = in_1;
  //   UEXT2__0[2:0] = UEXT1__0; WR = out_8
endmodule

module COMMON (
  input  CLK,
  input  RST,
  input  [7:0] DIN,
  input  [15:0] A,
  input  [15:0] ALU,
  input  [15:0] IVTPPDSP,
  input  [25:0] CMEMBUS,
  input  [15:0] in_8,
  input  [7:0] CFFBUS,
  input  [8:0] CREGBUS,
  input  [6:0] CPSW,
  output [15:0] MAR,
  output [7:0] MDR,
  output [3:0] PHASEFFBUS,
  output [15:0] out_15,
  output [7:0] out_16,
  output [15:0] out_17,
  output [10:0] INSTRUCBUS,
  output [7:0] out_19,
  output [7:0] out_20,
  output [7:0] out_21,
  output [3:0] ADDRBUS,
  output [7:0] out_23,
  output [15:0] out_24,
  output [15:0] PSW,
  output [7:0] out_26,
  output [1:0] out_27,
  output [15:0] B,
  output [19:0] out_29,
  output [2:0] out_30,
  output [15:0] out_31,
  output [7:0] out_32,
  output [7:0] out_33,
  output [6:0] out_34,
  output out_35
);

  wire A__0, ADDR, AdrIns, and_3_out, and_4_out, and_5_out, and_6_out, and_7_out, and_8_out, and_9_out,
       and_10_out, and_11_out, and_12_out, and_13_out, and_14_out, and_15_out, and_16_out, and_17_out,
       and_18_out, and_19_out, and_20_out, and_22_out, and_23_out, and_24_out, and_25_out, and_26_out,
       and_27_out, and_28_out, and_29_out, and_30_out, and_31_out, and_32_out, and_33_out, and_34_out, B__0,
       BezUslSkok, EXEC, FETCH, INTR, mp2_16b_1_p3, not_1_out, not_2_out, not_3_out, not_4_out, not_5_out,
       not_6_out, not_7_out, not_8_out, not_9_out, not_10_out, not_11_out, not_12_out, not_13_out,
       not_14_out, not_15_out, not_16_out, not_17_out, not_18_out, not_20_out, not_21_out, not_22_out,
       not_23_out, not_24_out, not_25_out, not_26_out, not_27_out, not_28_out, not_29_out, not_30_out,
       not_31_out, not_32_out, not_33_out, not_34_out, not_35_out, not_37_out, not_38_out, not_39_out,
       not_40_out, not_41_out, not_47_out, not_48_out, not_49_out, not_50_out, not_51_out, not_52_out,
       not_53_out, not_54_out, not_55_out, not_56_out, not_57_out, not_58_out, not_59_out, not_60_out,
       not_61_out, not_62_out, NulaAdrIns, or_2_out, or_3_out, or_4_out, or_5_out, or_6_out, or_7_out,
       reg8_1_p5, reg8_1_p6, reg16_inc_ld_2_p4, rsff_2_p4, rsff_3_p4, rsff_4_p4, rsff_9_p4, UslSkok;
  wire [7:0] AandB7__0, AandB15__8, multiplexer_2_out, multiplexer_4_out, multiplexer_5_out;
  wire [15:0] adder_1_out, multiplexer_3_out, multiplexer_6_out, multiplexer_7_out, PCIR, SP;

  // REG8_LD reg8_ld_1: pin names not known; wires that end beside it: CLK, MDR, out_21, CREGBUS[6]
  // REG16 reg16_1: pin names not known; wires that end beside it: CLK, {16{1'b0}}, SP, CREGBUS[0], CREGBUS[1], CREGBUS[2]
  Multiplexer #(.select(3), .width(16)) multiplexer_1 (
    .in0(out_24), .in1({out_20, out_19}), .in2(B), .in3(multiplexer_3_out), .in4(SP), .in5(IVTPPDSP),
    .out(out_15), .sel({CMEMBUS[20], CMEMBUS[6:5]}), .en(1'b1));  // open: in6, in7
  // REG16_INC_LD reg16_inc_ld_1: pin names not known; wires that end beside it: CLK, out_15, MAR, CMEMBUS[0], CMEMBUS[1]
  // REG8_LD reg8_ld_2: pin names not known; wires that end beside it: CLK, MDR, out_23, CREGBUS[7]
  // DC2_4 dc2_4_1: pin names not known; wires that end beside it: out_23[5:4], PSW[0], NulaAdrIns, UslSkok, BezUslSkok, AdrIns
  // DC3_8 dc3_8_1: pin names not known; wires that end beside it: out_21[6:4], AdrIns, out_34[6], out_34[1], out_34[5], out_34[0], out_34[4], out_34[3], out_34[2]
  Multiplexer #(.select(3), .width(8), .enable("false")) multiplexer_2 (
    .in0(out_20), .in1(out_31[15:8]), .in2(MDR), .in3(A[15:8]), .in4(AandB15__8), .out(multiplexer_2_out),
    .sel({CMEMBUS[24], CMEMBUS[8:7]}));  // open: in5, in6, in7
  // REG8 reg8_1: pin names not known; wires that end beside it: CLK, multiplexer_2_out, B[15:8], CMEMBUS[11], reg8_1_p5, reg8_1_p6
  assign {AandB15__8, AandB7__0} = B & A;  // AND_Gate and_1, 16 bits wide
  Multiplexer #(.width(16), .enable("false")) multiplexer_3 (
    .in0(out_31), .in1(adder_1_out), .out(multiplexer_3_out), .sel(out_34[2]));
  Adder #(.width(16)) adder_1 (.a({{9{out_19[7]}}, out_19[6:0]}), .b(out_31), .out(adder_1_out));  // open: cin, cout
  // REG8_LD reg8_ld_3: pin names not known; wires that end beside it: CLK, MDR, out_19, CREGBUS[5]
  Multiplexer #(.select(3), .width(8), .enable("false")) multiplexer_4 (
    .in0(out_19), .in1(out_31[7:0]), .in2(MDR), .in3(A[7:0]), .in4(AandB7__0), .out(multiplexer_4_out),
    .sel({CMEMBUS[23], CMEMBUS[10:9]}));  // open: in5, in6, in7
  // REG8 reg8_2: pin names not known; wires that end beside it: reg8_1_p5, reg8_1_p6, CLK, multiplexer_4_out, B[7:0], CMEMBUS[12], CMEMBUS[13], CMEMBUS[15]
  // DC3_8 dc3_8_2: pin names not known; wires that end beside it: out_23[2:0], NulaAdrIns, out_29[0], out_29[1], out_29[2], out_29[3], out_29[4], out_29[5], out_29[6]
  Multiplexer #(.select(3), .width(8), .enable("false")) multiplexer_5 (
    .in0(DIN), .in1(A[7:0]), .in2(A[15:8]), .in3(out_24[7:0]), .in4(out_24[15:8]), .in5(PSW[15:8]),
    .in6(PSW[7:0]), .out(multiplexer_5_out), .sel(CMEMBUS[19:17]));  // open: in7
  // REG8_LD reg8_ld_4: pin names not known; wires that end beside it: CLK, multiplexer_5_out, MDR, CMEMBUS[2]
  // REG8_LD reg8_ld_5: pin names not known; wires that end beside it: CLK, MDR, out_20, CREGBUS[4]
  // ADD16 add16_1: pin names not known; wires that end beside it: {{9{out_21[7]}}, out_21[6:0]}, PCIR, out_24
  // DC3_8 dc3_8_3: pin names not known; wires that end beside it: out_23[2:0], UslSkok, out_29[7], out_29[8], out_29[9], out_29[10], out_29[11]
  Multiplexer #(.width(16), .enable("false")) multiplexer_6 (
    .in0(B), .in1(A), .out(multiplexer_6_out), .sel(CMEMBUS[16]));
  Multiplexer #(.select(3), .width(16), .enable("false")) multiplexer_7 (
    .in0(MAR), .in1({out_19, out_21}), .in2(PCIR), .in3({MDR, out_24[7:0]}), .in4({out_24[15:8], MDR}),
    .out(multiplexer_7_out), .sel({CMEMBUS[25], CMEMBUS[22:21]}));  // open: in5, in6, in7
  // DC3_8 dc3_8_4: pin names not known; wires that end beside it: out_23[2:0], out_29[15], out_29[16], out_29[17], out_29[18], out_29[19]
  not not_1 (not_1_out, CMEMBUS[14]);
  not not_2 (not_2_out, RST);
  // RSFF rsff_1: pin names not known; wires that end beside it: CFFBUS[1], CLK, CFFBUS[0], not_2_out, FETCH
  // MP2_16b mp2_16b_1: pin names not known; wires that end beside it: RST, multiplexer_7_out, mp2_16b_1_p3, 16'h1000, 1'b1, in_8
  // REG16_INC_LD reg16_inc_ld_2: pin names not known; wires that end beside it: CLK, mp2_16b_1_p3, out_24, reg16_inc_ld_2_p4, CMEMBUS[4]
  // DC1_2 dc1_2_1: pin names not known; wires that end beside it: out_23[0], AdrIns, BezUslSkok, out_29[14], out_29[12], out_29[13]
  RAM_part #(.addrWidth(3), .dataWidth(16), .bus("separate")) ram_1 (
    .addr(out_21[3:1]), .din(multiplexer_6_out), .data(out_31), .str(CMEMBUS[14]), .sel(1'b1), .clk(CLK),
    .ld(not_1_out), .clr(1'b0));
  or or_1 (reg16_inc_ld_2_p4, CMEMBUS[3], RST);
  not not_3 (not_3_out, B[0]);
  not not_4 (not_4_out, B[1]);
  not not_5 (not_5_out, B[2]);
  not not_6 (not_6_out, B[3]);
  not not_7 (not_7_out, B[4]);
  not not_8 (not_8_out, B[5]);
  not not_9 (not_9_out, B[6]);
  not not_10 (not_10_out, B[7]);
  and and_2 (out_35, not_3_out, not_4_out, not_5_out, not_6_out, not_7_out, not_8_out, not_9_out, not_10_out, not_11_out, not_12_out, not_13_out, not_14_out, not_15_out, not_16_out, not_17_out, not_18_out);
  not not_11 (not_11_out, MDR[0]);
  not not_12 (not_12_out, MDR[1]);
  not not_13 (not_13_out, MDR[2]);
  not not_14 (not_14_out, MDR[3]);
  not not_15 (not_15_out, MDR[4]);
  not not_16 (not_16_out, MDR[5]);
  not not_17 (not_17_out, MDR[6]);
  not not_18 (not_18_out, MDR[7]);
  // RSFF rsff_2: pin names not known; wires that end beside it: CFFBUS[3], CLK, CFFBUS[2], rsff_2_p4, ADDR
  not not_19 (rsff_2_p4, RST);
  and and_3 (and_3_out, out_29[14], A__0);
  and and_4 (and_4_out, out_29[18], A__0);
  and and_5 (and_5_out, out_29[6], A__0);
  and and_6 (and_6_out, out_29[3], A__0);
  and and_7 (and_7_out, out_29[19], A__0);
  and and_8 (and_8_out, out_29[17], B__0);
  and and_9 (and_9_out, out_29[2], MDR[1]);
  and and_10 (and_10_out, MDR[1], out_29[4]);
  or or_2 (or_2_out, out_29[2], out_29[4]);
  or or_3 (or_3_out, out_29[2], out_29[4]);
  and and_11 (and_11_out, or_4_out, MDR[0]);
  or or_4 (or_4_out, out_29[4], out_29[2]);
  and and_12 (and_12_out, A[15], out_29[14]);
  and and_13 (and_13_out, A[15], out_29[6]);
  and and_14 (and_14_out, A[15], out_29[18]);
  and and_15 (and_15_out, out_29[17], B[15]);
  and and_16 (and_16_out, out_29[2], out_29[4]);
  and and_17 (and_17_out, and_16_out, MDR[1]);
  and and_18 (and_18_out, or_2_out, MDR[4]);
  and and_19 (and_19_out, or_3_out, MDR[7]);
  and and_20 (and_20_out, out_29[3], A[7]);
  not not_20 (not_20_out, A[0]);
  not not_21 (not_21_out, A[1]);
  not not_22 (not_22_out, A[2]);
  not not_23 (not_23_out, A[3]);
  not not_24 (not_24_out, A[4]);
  not not_25 (not_25_out, A[5]);
  not not_26 (not_26_out, A[6]);
  not not_27 (not_27_out, A[7]);
  and and_21 (A__0, not_20_out, not_21_out, not_22_out, not_23_out, not_24_out, not_25_out, not_26_out, not_27_out, not_28_out, not_29_out, not_30_out, not_31_out, not_32_out, not_33_out, not_34_out, not_35_out);
  not not_28 (not_28_out, A[8]);
  not not_29 (not_29_out, A[9]);
  not not_30 (not_30_out, A[10]);
  not not_31 (not_31_out, A[11]);
  not not_32 (not_32_out, A[12]);
  not not_33 (not_33_out, A[13]);
  not not_34 (not_34_out, A[14]);
  not not_35 (not_35_out, A[15]);
  // RSFF rsff_3: pin names not known; wires that end beside it: CFFBUS[5], CLK, CFFBUS[4], rsff_3_p4, EXEC
  not not_36 (rsff_3_p4, RST);
  not not_37 (not_37_out, or_5_out);
  or or_5 (or_5_out, and_3_out, and_4_out, and_5_out, and_6_out, and_7_out, and_8_out, and_9_out, and_10_out);
  or or_6 (or_6_out, and_12_out, and_13_out, and_14_out, and_15_out, and_17_out);
  or or_7 (or_7_out, and_19_out, and_20_out);
  not not_38 (not_38_out, or_7_out);
  and and_22 (and_22_out, MDR[7], out_29[2]);
  not not_39 (not_39_out, and_22_out);
  and and_23 (and_23_out, and_11_out, CPSW[1]);
  and and_24 (and_24_out, not_37_out, CPSW[2]);
  and and_25 (and_25_out, or_5_out, CPSW[2]);
  not not_40 (not_40_out, or_6_out);
  and and_26 (and_26_out, not_40_out, CPSW[3]);
  and and_27 (and_27_out, or_6_out, CPSW[3]);
  not not_41 (not_41_out, and_18_out);
  and and_28 (and_28_out, not_41_out, CPSW[4]);
  and and_29 (and_29_out, and_18_out, CPSW[4]);
  and and_30 (and_30_out, not_38_out, CPSW[5]);
  and and_31 (and_31_out, or_7_out, CPSW[5]);
  and and_32 (and_32_out, not_39_out, CPSW[6]);
  and and_33 (and_33_out, and_22_out, CPSW[6]);
  and and_34 (and_34_out, CPSW[1], out_29[0]);
  // RSFF rsff_4: pin names not known; wires that end beside it: and_24_out, CLK, and_25_out, rsff_4_p4, PSW[1]
  not not_42 (rsff_4_p4, RST);
  // RSFF rsff_5: pin names not known; wires that end beside it: and_26_out, CLK, and_27_out, PSW[2]
  // NOT_Gate not_43 has open pins: in=RST, out=open
  // RSFF rsff_6: pin names not known; wires that end beside it: and_28_out, CLK, and_29_out, PSW[3]
  // NOT_Gate not_44 has open pins: in=RST, out=open
  // RSFF rsff_7: pin names not known; wires that end beside it: and_30_out, CLK, and_31_out, PSW[4]
  // NOT_Gate not_45 has open pins: in=RST, out=open
  // RSFF rsff_8: pin names not known; wires that end beside it: and_32_out, CLK, and_33_out, PSW[15]
  // NOT_Gate not_46 has open pins: in=RST, out=open
  not not_47 (not_47_out, B[0]);
  not not_48 (not_48_out, B[1]);
  not not_49 (not_49_out, B[2]);
  not not_50 (not_50_out, B[3]);
  not not_51 (not_51_out, B[4]);
  not not_52 (not_52_out, B[5]);
  not not_53 (not_53_out, B[6]);
  not not_54 (not_54_out, B[7]);
  and and_35 (B__0, not_47_out, not_48_out, not_49_out, not_50_out, not_51_out, not_52_out, not_53_out, not_54_out, not_55_out, not_56_out, not_57_out, not_58_out, not_59_out, not_60_out, not_61_out, not_62_out);
  not not_55 (not_55_out, B[8]);
  not not_56 (not_56_out, B[9]);
  not not_57 (not_57_out, B[10]);
  not not_58 (not_58_out, B[11]);
  not not_59 (not_59_out, B[12]);
  not not_60 (not_60_out, B[13]);
  not not_61 (not_61_out, B[14]);
  not not_62 (not_62_out, B[15]);
  // RSFF rsff_9: pin names not known; wires that end beside it: CFFBUS[7], CLK, CFFBUS[6], rsff_9_p4, INTR
  not not_63 (rsff_9_p4, RST);
  // NOT_Gate not_64 has open pins: in=RST, out=open
  // RSFF rsff_10: pin names not known; wires that end beside it: and_34_out, CLK, and_23_out, PSW[0]
  assign PHASEFFBUS[3] = INTR ? 1'b1 : 1'bz;  // Controlled_Buffer controlled_buffer_1
  assign PHASEFFBUS[1] = ADDR ? 1'b1 : 1'bz;  // Controlled_Buffer controlled_buffer_2
  assign PHASEFFBUS[2] = EXEC ? 1'b1 : 1'bz;  // Controlled_Buffer controlled_buffer_3
  assign PHASEFFBUS[0] = FETCH ? 1'b1 : 1'bz;  // Controlled_Buffer controlled_buffer_4

  assign out_16 = MDR;
  assign out_17 = MAR;
  assign out_26 = out_23;
  assign out_27 = out_23[5:4];
  assign out_30 = out_21[3:1];
  assign out_32 = B[15:8];
  assign out_33 = B[7:0];

  // Other names for the same wires on the sheet: B1MUX0 = CMEMBUS[7]; B1MUX1 = CMEMBUS[8]; B1MUX2 = CMEMBUS[24];
  //   MARMX0 = CMEMBUS[5]; MARMX1 = CMEMBUS[6]; MARMX2 = CMEMBUS[20]; IR7__0[7:0] = out_20; B0MUX0 = CMEMBUS[9];
  //   B0MUX1 = CMEMBUS[10]; B0MUX2 = CMEMBUS[23]; MDRMX0 = CMEMBUS[17]; MDRMX1 = CMEMBUS[18]; MDRMX2 = CMEMBUS[19];
  //   PCMUX0 = CMEMBUS[21]; PCMUX1 = CMEMBUS[22]; PCMUX2 = CMEMBUS[25]; IR23__16[7:0] = out_21; IR15__8[7:0] = out_19;
  //   MDR7__0[7:0] = MDR; B7__0[7:0] = B[7:0]; B15__8[7:0] = B[15:8]; BMDR__0 = out_35; stFETCH = CFFBUS[0];
  //   clFETCH = CFFBUS[1]; stADDR = CFFBUS[2]; clADDR = CFFBUS[3]; stEXEC = CFFBUS[4]; clEXEC = CFFBUS[5];
  //   stINTR = CFFBUS[6]; clINTR = CFFBUS[7]; ldMAR = CMEMBUS[0]; incMAR = CMEMBUS[1]; ldMDR = CMEMBUS[2];
  //   ldPC = CMEMBUS[3]; incPC = CMEMBUS[4]; ldB15__8 = CMEMBUS[11]; ldB7__0 = CMEMBUS[12]; incB = CMEMBUS[13];
  //   ldR = CMEMBUS[14]; decB = CMEMBUS[15]; RMUX = CMEMBUS[16]; clPSWSTART = CPSW[0]; stPSWSTART = CPSW[1];
  //   ldZ = CPSW[2]; ldN = CPSW[3]; ldC = CPSW[4]; ldV = CPSW[5]; ldI = CPSW[6]; ldSP = CREGBUS[0];
  //   incSP = CREGBUS[1]; decSP = CREGBUS[2]; ldIR7__0 = CREGBUS[4]; ldIR15__8 = CREGBUS[5]; ldIR23__16 = CREGBUS[6];
  //   ldIR31__24 = CREGBUS[7]; Din7__0[7:0] = DIN; ENTRADDR15__0[15:0] = IVTPPDSP; inPC[15:0] = in_8;
  //   IR31__24[7:0] = out_23; MAR15__0[15:0] = MAR; HALT = out_29[0]; RTS = out_29[1]; RTI = out_29[2];
  //   ASL = out_29[3]; POPPSW = out_29[4]; PUSH = out_29[5]; POP = out_29[6]; BEQL = out_29[7]; BNEQ = out_29[8];
  //   BLEQU = out_29[9]; BLSS = out_29[10]; JLEQ = out_29[11]; JMP = out_29[12]; JSP = out_29[13]; LD = out_29[14];
  //   ST = out_29[15]; JADR = out_29[16]; TST = out_29[17]; XOR = out_29[18]; STRLEN = out_29[19]; memind = out_34[0];
  //   memdir = out_34[1]; regindpom = out_34[2]; postinc = out_34[3]; preinc = out_34[4]; regdir = out_34[5];
  //   immed = out_34[6]; PC15__0[15:0] = out_24; PSW7__0[15:0] = PSW; PSWSTART = PSW[0]; PSWZ = PSW[1]; PSWN = PSW[2];
  //   PSWC = PSW[3]; PSWV = PSW[4]; PSWI = PSW[15]; R[15:0] = out_31

  // Notes on the sheet:
  //   Instrukcijski registar
  //   ПОМОЋНИ РЕГИСТАР
  //   SP
  //   MAR
  //   Dekoderi za prepoznavanje instrukcije na osnovu sadrzaja registra IR23..16
  //   MDR
  //   PC
  //   FF za pokretanje FETCH, ADDR, EXEC i INTR faze izvršavanja instrukcije
  //   Programska statusna reč (PSW)
endmodule

module FETCH (
  input  in_1,
  input  in_2,
  input  in_3,
  input  [3:0] PHASEFFBUS,
  input  [10:0] INSTRUCBUS,
  input  [3:0] ADDRBUS,
  input  [15:0] PSW,
  input  [19:0] in_8,
  input  [6:0] in_9,
  output [25:0] CMEMBUS,
  output [7:0] CFFBUS,
  output [4:0] out_12,
  output [8:0] CREGBUS,
  output [7:0] out_14,
  output rdMEM
);

  wire addr2, addr3, addr_t, adr2S, adr3S, and_1_out, and_2_out, and_3_out, and_4_out, and_5_out, and_6_out,
       and_7_out, and_8_out, and_9_out, and_10_out, and_11_out, bezadr, bezadresne, brcnd, bruncnd, clFETCH,
       FCBUSS, FETCHnPSWSTART, gradr, gradrS, grinst, grinstS, incPC, jmp2, jmp2S, jmp3, jmp3S, ldIR7__0,
       ldIR15__8, ldIR23__16, ldIR31__24, ldMAR, ldMDR, not_3_out, not_4_out, not_5_out, or_4_out, or_8_out,
       or_9_out, or_10_out, rdMEM_t, reg8_inc_ld_1_p3, reg8_inc_ld_1_p4, stADDR, stEXEC, stFETCH;
  wire [3:0] rom_1_data;
  wire [7:0] multiplexer_1_out;
  wire [7:5] rom_1_data_2;

  or or_1 (jmp3, in_8[12], in_8[13], in_8[11]);
  or or_2 (jmp2, in_8[7], in_8[8], in_8[9], in_8[10]);
  Decoder #(.select(4), .enable("false")) decoder_1 (
    .out1(FETCHnPSWSTART), .out2(FCBUSS), .out3(bezadr), .out4(grinstS), .out5(jmp2S), .out6(gradrS),
    .out7(adr2S), .out8(jmp3S), .out9(adr3S), .out10(bruncnd), .sel(rom_1_data));  // open: out0, out11, out12, out13, out14, out15
  or or_3 (bezadresne, in_8[0], in_8[1], in_8[2], in_8[3], in_8[4], in_8[5], in_8[6]);
  Multiplexer #(.width(8), .enable("false")) multiplexer_1 (
    .in0({3'b000, out_14[4:0]}), .in1({8{1'b0}}), .out(multiplexer_1_out), .sel(in_1));
  // REG8_INC_LD reg8_inc_ld_1: pin names not known; wires that end beside it: in_2, multiplexer_1_out, reg8_inc_ld_1_p3, reg8_inc_ld_1_p4
  not not_1 (reg8_inc_ld_1_p4, reg8_inc_ld_1_p3);
  and and_1 (and_1_out, in_9[6], or_4_out);
  or or_4 (or_4_out, in_8[15], in_8[16]);
  and and_2 (and_2_out, in_8[16], in_9[2]);
  or or_5 (reg8_inc_ld_1_p3, bruncnd, brcnd);
  ROM #(.addrWidth(5), .dataWidth(24)) rom_1 (
    .addr(out_12),
    .data({ldMAR, incPC, ldMDR, rdMEM_t, ldIR31__24, ldIR23__16, ldIR15__8, ldIR7__0, clFETCH, stADDR, stEXEC, stFETCH, rom_1_data, rom_1_data_2, out_14[4:0]}),
    .sel(1'b1));
  or or_6 (addr_t, in_8[14], in_8[15], in_8[16], in_8[17], in_8[18], in_8[19]);
  or or_7 (gradr, and_1_out, and_2_out);
  or or_8 (or_8_out, in_8[0], in_8[1], in_8[2], in_8[3], in_8[4], in_8[5], in_8[6], in_8[7], in_8[8], in_8[9], in_8[10], in_8[11], in_8[12], in_8[13], in_8[14], in_8[15], in_8[16], in_8[17], in_8[18], in_8[19]);
  not not_2 (grinst, or_8_out);
  not not_3 (not_3_out, PHASEFFBUS[0]);
  not not_4 (not_4_out, PSW[0]);
  or or_9 (or_9_out, not_3_out, not_4_out);
  and and_3 (and_3_out, or_9_out, FETCHnPSWSTART);
  and and_4 (and_4_out, FCBUSS, not_5_out);
  not not_5 (not_5_out, in_3);
  and and_5 (and_5_out, bezadr, bezadresne);
  and and_6 (and_6_out, grinstS, grinst);
  and and_7 (and_7_out, jmp2S, jmp2);
  and and_8 (and_8_out, gradrS, gradr);
  and and_9 (and_9_out, adr2S, addr2);
  and and_10 (and_10_out, jmp3S, jmp3);
  and and_11 (and_11_out, adr3S, addr3);
  and and_12 (addr3, in_9[2], addr_t);
  or or_10 (or_10_out, in_9[5], in_9[3], in_9[4]);
  and and_13 (addr2, or_10_out, addr_t);
  or or_11 (brcnd, and_3_out, and_4_out, and_5_out, and_6_out, and_7_out, and_8_out, and_9_out, and_10_out, and_11_out);
  assign CMEMBUS[4] = incPC ? 1'b1 : 1'bz;  // Controlled_Buffer controlled_buffer_1
  assign CREGBUS[4] = ldIR7__0 ? 1'b1 : 1'bz;  // Controlled_Buffer controlled_buffer_2
  assign CREGBUS[5] = ldIR15__8 ? 1'b1 : 1'bz;  // Controlled_Buffer controlled_buffer_3
  assign CREGBUS[6] = ldIR23__16 ? 1'b1 : 1'bz;  // Controlled_Buffer controlled_buffer_4
  assign CREGBUS[7] = ldIR31__24 ? 1'b1 : 1'bz;  // Controlled_Buffer controlled_buffer_5
  assign CMEMBUS[2] = ldMDR ? 1'b1 : 1'bz;  // Controlled_Buffer controlled_buffer_6
  assign CFFBUS[2] = stADDR ? 1'b1 : 1'bz;  // Controlled_Buffer controlled_buffer_7
  assign CFFBUS[4] = stEXEC ? 1'b1 : 1'bz;  // Controlled_Buffer controlled_buffer_8
  assign CMEMBUS[0] = ldMAR ? 1'b1 : 1'bz;  // Controlled_Buffer controlled_buffer_9
  assign CFFBUS[0] = stFETCH ? 1'b1 : 1'bz;  // Controlled_Buffer controlled_buffer_10
  assign CFFBUS[1] = clFETCH ? 1'b1 : 1'bz;  // Controlled_Buffer controlled_buffer_11
  assign rdMEM = rdMEM_t ? 1'b1 : 1'bz;  // Controlled_Buffer controlled_buffer_12

  assign out_14[7:5] = 3'b000;

  // Other names for the same wires on the sheet: CLK = in_2; FCBUS = in_3; HALT = in_8[0]; RTS = in_8[1];
  //   RTI = in_8[2]; ASL = in_8[3]; POPPSW = in_8[4]; PUSH = in_8[5]; POP = in_8[6]; BEQL = in_8[7]; BNEQ = in_8[8];
  //   BLEQU = in_8[9]; BLSS = in_8[10]; JLEQ = in_8[11]; JMP = in_8[12]; JSP = in_8[13]; LD = in_8[14]; ST = in_8[15];
  //   JADR = in_8[16]; TST = in_8[17]; XOR = in_8[18]; STRLEN = in_8[19]; memind = in_9[0]; memdir = in_9[1];
  //   regindpom = in_9[2]; postinc = in_9[3]; preinc = in_9[4]; regdir = in_9[5]; immed = in_9[6];
  //   FETCH = PHASEFFBUS[0]; ADDR = PHASEFFBUS[1]; EXEC = PHASEFFBUS[2]; INTR = PHASEFFBUS[3]; PSWSTART = PSW[0];
  //   rst = in_1

  // Notes on the sheet:
  //   Operaciona jedinica
  //   Kontrolna jedinica
  //   contents of rom_1 (hex, n*v repeats v):
  //   100 c00000 300202 80000 313 400 c00000 300207 40513 600 712 c00000 30020c 20813 912 c00000 300210
  //   10000 ca00 aa00 1a00
endmodule

module ADDR (
  input  in_1,
  input  in_2,
  input  in_3,
  input  [3:0] PHASEFFBUS,
  input  [10:0] INSTRUCBUS,
  input  [3:0] ADDRBUS,
  input  [19:0] in_7,
  input  [6:0] in_8,
  output [25:0] CMEMBUS,
  output [7:0] CFFBUS,
  output [7:0] out_11,
  output [8:0] CREGBUS,
  output rdMEM
);

  wire ADDRc, and_1_out, and_2_out, and_3_out, and_4_out, B0MUX0, B0MUX1, B1MUX0, B1MUX1, branchADR, brcnd,
       brunchnd, clADDR, decB, FCBUSc, incB, incMAR, ldB7__0, ldB15__8, ldMAR, ldMDR, ldR, MARMX0, MARMX1,
       not_2_out, not_3_out, or_2_out, rdMEM_t, reg8_inc_ld_1_p3, reg8_inc_ld_1_p4, stEXEC, STOREc,
       STRLEN_ST_JADR;
  wire [3:0] rom_1_data;
  wire [4:0] kaddrmx_1_adr4__0, multiplexer_1_out, rom_1_data_2;

  Decoder #(.select(4), .enable("false")) decoder_1 (
    .out1(brunchnd), .out2(ADDRc), .out3(branchADR), .out4(STOREc), .out5(FCBUSc), .out6(STRLEN_ST_JADR),
    .sel(rom_1_data));  // open: out0, out7, out8, out9, out10, out11, out12, out13, out14, out15
  KADDRMX kaddrmx_1 (
    .immed(in_8[6]), .regdir(in_8[5]), .memdir(in_8[1]), .memind(in_8[0]), .preinc(in_8[4]),
    .postinc(in_8[3]), .regindpom(in_8[2]), .Adr4__0(kaddrmx_1_adr4__0));
  Multiplexer #(.width(5), .disabled(0), .enable("false")) multiplexer_1 (
    .in0(rom_1_data_2), .in1(kaddrmx_1_adr4__0), .out(multiplexer_1_out), .sel(branchADR));
  // REG8_INC_LD reg8_inc_ld_1: pin names not known; wires that end beside it: in_2, out_11, reg8_inc_ld_1_p3, reg8_inc_ld_1_p4
  not not_1 (reg8_inc_ld_1_p4, reg8_inc_ld_1_p3);
  or or_1 (reg8_inc_ld_1_p3, brcnd, brunchnd, branchADR);
  ROM #(.addrWidth(5), .dataWidth(26)) rom_1 (
    .addr(out_11[4:0]),
    .data({rom_1_data_2[0], rom_1_data_2[1], rom_1_data_2[2], rom_1_data_2[3], rom_1_data_2[4], rom_1_data[0], rom_1_data[1], rom_1_data[2], rom_1_data[3], decB, clADDR, rdMEM_t, stEXEC, ldR, ldMDR, MARMX1, MARMX0, incMAR, ldMAR, incB, B1MUX1, B1MUX0, B0MUX1, B0MUX0, ldB15__8, ldB7__0}),
    .sel(1'b1));
  or or_2 (or_2_out, in_7[15], in_7[19], in_7[16]);
  and and_1 (and_1_out, ADDRc, not_2_out);
  not not_2 (not_2_out, PHASEFFBUS[1]);
  and and_2 (and_2_out, STOREc, in_7[15]);
  and and_3 (and_3_out, FCBUSc, not_3_out);
  not not_3 (not_3_out, in_3);
  and and_4 (and_4_out, STRLEN_ST_JADR, or_2_out);
  or or_3 (brcnd, and_1_out, and_2_out, and_3_out, and_4_out);
  assign CMEMBUS[6] = MARMX1 ? 1'b1 : 1'bz;  // Controlled_Buffer controlled_buffer_1
  assign CMEMBUS[7] = B1MUX0 ? 1'b1 : 1'bz;  // Controlled_Buffer controlled_buffer_2
  assign CMEMBUS[8] = B1MUX1 ? 1'b1 : 1'bz;  // Controlled_Buffer controlled_buffer_3
  assign CMEMBUS[9] = B0MUX0 ? 1'b1 : 1'bz;  // Controlled_Buffer controlled_buffer_4
  assign CMEMBUS[10] = B0MUX1 ? 1'b1 : 1'bz;  // Controlled_Buffer controlled_buffer_5
  assign CMEMBUS[11] = ldB15__8 ? 1'b1 : 1'bz;  // Controlled_Buffer controlled_buffer_6
  assign CMEMBUS[12] = ldB7__0 ? 1'b1 : 1'bz;  // Controlled_Buffer controlled_buffer_7
  assign CMEMBUS[13] = incB ? 1'b1 : 1'bz;  // Controlled_Buffer controlled_buffer_8
  assign CMEMBUS[14] = ldR ? 1'b1 : 1'bz;  // Controlled_Buffer controlled_buffer_9
  assign CMEMBUS[15] = decB ? 1'b1 : 1'bz;  // Controlled_Buffer controlled_buffer_10
  assign CMEMBUS[2] = ldMDR ? 1'b1 : 1'bz;  // Controlled_Buffer controlled_buffer_11
  assign CFFBUS[3] = clADDR ? 1'b1 : 1'bz;  // Controlled_Buffer controlled_buffer_12
  assign CFFBUS[4] = stEXEC ? 1'b1 : 1'bz;  // Controlled_Buffer controlled_buffer_13
  assign CMEMBUS[0] = ldMAR ? 1'b1 : 1'bz;  // Controlled_Buffer controlled_buffer_14
  assign CMEMBUS[1] = incMAR ? 1'b1 : 1'bz;  // Controlled_Buffer controlled_buffer_15
  assign CMEMBUS[5] = MARMX0 ? 1'b1 : 1'bz;  // Controlled_Buffer controlled_buffer_16
  assign rdMEM = rdMEM_t ? 1'b1 : 1'bz;  // Controlled_Buffer controlled_buffer_17

  // Other names for the same wires on the sheet: CLK = in_2; FCBUS = in_3; HALT = in_7[0]; RTS = in_7[1];
  //   RTI = in_7[2]; ASL = in_7[3]; POPPSW = in_7[4]; PUSH = in_7[5]; POP = in_7[6]; BEQL = in_7[7]; BNEQ = in_7[8];
  //   BLEQU = in_7[9]; BLSS = in_7[10]; JLEQ = in_7[11]; JMP = in_7[12]; JSP = in_7[13]; LD = in_7[14]; ST = in_7[15];
  //   JADR = in_7[16]; TST = in_7[17]; XOR = in_7[18]; STRLEN = in_7[19]; memind = in_8[0]; memdir = in_8[1];
  //   regindpom = in_8[2]; postinc = in_8[3]; preinc = in_8[4]; regdir = in_8[5]; immed = in_8[6];
  //   FETCH = PHASEFFBUS[0]; ADDR = PHASEFFBUS[1]; EXEC = PHASEFFBUS[2]; INTR = PHASEFFBUS[3]; rst = in_1

  // Notes on the sheet:
  //   Upravljacka jedinica
  //   Operaciona jedinica
  //   contents of rom_1 (hex, n*v repeats v):
  //   80000 180000 1700003 1640000 1700017 2b00280 280 3944800 109 2544800 22 2b00480 17 40 40 2b01480 697
  //   10000 10000 2b01000 2a00680 16c0000 1b44800 109 744800 22 10a000
endmodule

module EXEC (
  input  in_1,
  input  in_2,
  input  in_3,
  input  [15:0] B,
  input  [3:0] PHASEFFBUS,
  input  [10:0] INSTRUCBUS,
  input  [3:0] ADDRBUS,
  input  [15:0] PSW,
  input  [19:0] in_9,
  input  [6:0] in_10,
  input  in_11,
  output [15:0] A,
  output [15:0] ALU,
  output [25:0] CMEMBUS,
  output [15:0] out_15,
  output [15:0] out_16,
  output [7:0] CFFBUS,
  output [8:0] CREGBUS,
  output [6:0] CPSW,
  output rdMEM,
  output wrMEM
);

  wire AMUX0, and_1_out, and_2_out, and_3_out, and_4_out, and_5_out, and_6_out, and_7_out, and_8_out,
       and_9_out, and_10_out, and_11_out, and_12_out, and_13_out, B0MUX1, B0MUX2, B1MUX1, B1MUX2, BMDRc,
       branchEXEC, brcnd, brunchnd, clA, decSP, EXECc, FCBUSc, incA, incMAR, incSP, ldA, ldB7__0, ldB15__8,
       ldMAR, ldMDR, ldPC, ldR, MARMX2, MDRMX0, MDRMX1, MDRMX2, not_2_out, not_3_out, not_4_out, not_5_out,
       not_6_out, not_7_out, or_1_out, or_2_out, or_3_out, or_5_out, or_6_out, or_7_out, PCMUX0, PCMUX1,
       PCMUX2, POPPSWc, rdMEM_t, reg16_inc_ld_1_p3, reg16_inc_ld_1_p4, REGDIRc, RMUX, RTSc, slA, uslov1,
       uslov2, wrMEM_t, xor_2_out, xor_3_out;
  wire [3:0] rom_1_data_2;
  wire [5:0] kexecmx_1_adr4__0, multiplexer_2_out, rom_1_data_3;
  wire [7:4] rom_1_data;
  wire [15:0] multiplexer_1_out, xor_1_out;

  or or_1 (or_1_out, in_1, clA);
  KEXECMX kexecmx_1 (
    .HALT(in_9[0]), .PUSH(in_9[5]), .LD(in_9[14]), .RTI_POPPSW(or_2_out), .RTS(in_9[1]), .POP(in_9[6]),
    .skok2(or_3_out), .JLEQ(in_9[13]), .JSR(in_9[11]), .JMP(in_9[12]), .TST(in_9[17]), .ASL(in_9[3]),
    .XOR(in_9[18]), .JADR(in_9[16]), .STRLEN(in_9[19]), .STORE(in_9[15]), .Adr4__0(kexecmx_1_adr4__0));
  Decoder #(.select(4), .enable("false")) decoder_1 (
    .out1(brunchnd), .out2(EXECc), .out3(branchEXEC), .out4(FCBUSc), .out5(POPPSWc), .out6(RTSc),
    .out7(uslov1), .out8(uslov2), .out9(REGDIRc), .out10(BMDRc), .sel(rom_1_data_2));  // open: out0, out11, out12, out13, out14, out15
  assign xor_1_out = B ^ A;  // XOR_Gate xor_1, 16 bits wide
  Multiplexer #(.width(16), .enable("false")) multiplexer_1 (
    .in0(B), .in1(xor_1_out), .out(multiplexer_1_out), .sel(AMUX0));
  // REG16 reg16_1: pin names not known; wires that end beside it: or_1_out, in_2, multiplexer_1_out, A, ldA, slA, 1'b0, incA
  or or_2 (or_2_out, in_9[4], in_9[2]);
  or or_3 (or_3_out, in_9[9], in_9[7], in_9[10], in_9[8]);
  Multiplexer #(.width(6), .disabled(0), .enable("false")) multiplexer_2 (
    .in0(rom_1_data_3), .in1(kexecmx_1_adr4__0), .out(multiplexer_2_out), .sel(branchEXEC));
  // REG16_INC_LD reg16_inc_ld_1: pin names not known; wires that end beside it: in_2, out_16, reg16_inc_ld_1_p3, reg16_inc_ld_1_p4
  ROM #(.addrWidth(6), .dataWidth(18)) rom_1 (
    .addr(out_16[5:0]),
    .data({rom_1_data_3[0], rom_1_data_3[1], rom_1_data_3[2], rom_1_data_3[3], rom_1_data_3[4], rom_1_data_3[5], rom_1_data_2[0], rom_1_data_2[1], rom_1_data_2[2], rom_1_data_2[3], rom_1_data, CFFBUS[6:5], rdMEM_t, wrMEM_t}),
    .sel(1'b1));
  not not_1 (reg16_inc_ld_1_p4, reg16_inc_ld_1_p3);
  or or_4 (reg16_inc_ld_1_p3, brcnd, brunchnd, branchEXEC);
  ROM #(.addrWidth(6), .dataWidth(32)) rom_2 (
    .addr(out_16[5:0]),
    .data({RMUX, ldR, PCMUX2, PCMUX1, PCMUX0, ldPC, MDRMX2, MDRMX1, MDRMX0, ldMDR, MARMX2, incMAR, ldMAR, B1MUX2, B0MUX2, B1MUX1, B0MUX1, ldB15__8, ldB7__0, decSP, incSP, AMUX0, incA, slA, clA, ldA, CPSW[5:4], CPSW[6], CPSW[2], CPSW[3], CPSW[1]}),
    .sel(1'b1));
  not not_2 (not_2_out, PSW[1]);
  and and_1 (and_1_out, EXECc, not_3_out);
  not not_3 (not_3_out, PHASEFFBUS[2]);
  not not_4 (not_4_out, in_3);
  and and_2 (and_2_out, not_4_out, FCBUSc);
  and and_3 (and_3_out, POPPSWc, in_9[4]);
  and and_4 (and_4_out, RTSc, in_9[1]);
  and and_5 (and_5_out, REGDIRc, not_5_out);
  not not_5 (not_5_out, in_10[5]);
  and and_6 (and_6_out, in_9[7], PSW[1]);
  and and_7 (and_7_out, in_9[8], not_2_out);
  and and_8 (and_8_out, in_9[9], or_5_out);
  or or_5 (or_5_out, PSW[3], PSW[1]);
  and and_9 (and_9_out, in_9[10], xor_2_out);
  xor xor_2 (xor_2_out, PSW[2], PSW[4]);
  or or_6 (or_6_out, PSW[1], xor_3_out);
  xor xor_3 (xor_3_out, PSW[2], PSW[4]);
  and and_10 (and_10_out, BMDRc, in_11);
  not not_6 (not_6_out, or_7_out);
  or or_7 (or_7_out, and_6_out, and_7_out, and_8_out, and_9_out);
  and and_11 (and_11_out, in_9[11], or_6_out);
  not not_7 (not_7_out, and_11_out);
  and and_12 (and_12_out, uslov1, not_6_out);
  and and_13 (and_13_out, uslov2, not_7_out);
  or or_8 (brcnd, and_1_out, and_2_out, and_3_out, and_4_out, and_5_out, and_10_out, and_12_out, and_13_out);
  assign CMEMBUS[0] = ldMAR ? 1'b1 : 1'bz;  // Controlled_Buffer controlled_buffer_1
  assign CMEMBUS[1] = incMAR ? 1'b1 : 1'bz;  // Controlled_Buffer controlled_buffer_2
  assign CMEMBUS[2] = ldMDR ? 1'b1 : 1'bz;  // Controlled_Buffer controlled_buffer_3
  assign CMEMBUS[3] = ldPC ? 1'b1 : 1'bz;  // Controlled_Buffer controlled_buffer_4
  assign CMEMBUS[8] = B1MUX1 ? 1'b1 : 1'bz;  // Controlled_Buffer controlled_buffer_5
  assign CMEMBUS[10] = B0MUX1 ? 1'b1 : 1'bz;  // Controlled_Buffer controlled_buffer_6
  assign CMEMBUS[11] = ldB15__8 ? 1'b1 : 1'bz;  // Controlled_Buffer controlled_buffer_7
  assign CMEMBUS[12] = ldB7__0 ? 1'b1 : 1'bz;  // Controlled_Buffer controlled_buffer_8
  assign CMEMBUS[14] = ldR ? 1'b1 : 1'bz;  // Controlled_Buffer controlled_buffer_9
  assign CMEMBUS[16] = RMUX ? 1'b1 : 1'bz;  // Controlled_Buffer controlled_buffer_10
  assign CMEMBUS[17] = MDRMX0 ? 1'b1 : 1'bz;  // Controlled_Buffer controlled_buffer_11
  assign CMEMBUS[18] = MDRMX1 ? 1'b1 : 1'bz;  // Controlled_Buffer controlled_buffer_12
  assign CMEMBUS[19] = MDRMX2 ? 1'b1 : 1'bz;  // Controlled_Buffer controlled_buffer_13
  assign CMEMBUS[20] = MARMX2 ? 1'b1 : 1'bz;  // Controlled_Buffer controlled_buffer_14
  assign CMEMBUS[21] = PCMUX0 ? 1'b1 : 1'bz;  // Controlled_Buffer controlled_buffer_15
  assign CMEMBUS[22] = PCMUX1 ? 1'b1 : 1'bz;  // Controlled_Buffer controlled_buffer_16
  assign CMEMBUS[23] = B0MUX2 ? 1'b1 : 1'bz;  // Controlled_Buffer controlled_buffer_17
  assign CMEMBUS[24] = B1MUX2 ? 1'b1 : 1'bz;  // Controlled_Buffer controlled_buffer_18
  assign CMEMBUS[25] = PCMUX2 ? 1'b1 : 1'bz;  // Controlled_Buffer controlled_buffer_19
  assign CREGBUS[1] = incSP ? 1'b1 : 1'bz;  // Controlled_Buffer controlled_buffer_20
  assign CREGBUS[2] = decSP ? 1'b1 : 1'bz;  // Controlled_Buffer controlled_buffer_21
  assign rdMEM = rdMEM_t ? 1'b1 : 1'bz;  // Controlled_Buffer controlled_buffer_22
  assign wrMEM = wrMEM_t ? 1'b1 : 1'bz;  // Controlled_Buffer controlled_buffer_23

  assign out_15 = A;

  // Other names for the same wires on the sheet: BMDR = in_11; clEXEC = CFFBUS[5]; stINTR = CFFBUS[6]; CLK = in_2;
  //   stPSWSTART = CPSW[1]; ldZ = CPSW[2]; ldN = CPSW[3]; ldC = CPSW[4]; ldV = CPSW[5]; ldI = CPSW[6]; FCBUS = in_3;
  //   HALT = in_9[0]; RTS = in_9[1]; RTI = in_9[2]; ASL = in_9[3]; POPPSW = in_9[4]; PUSH = in_9[5]; POP = in_9[6];
  //   BEQL = in_9[7]; BNEQ = in_9[8]; BLEQU = in_9[9]; BLSS = in_9[10]; JLEQ = in_9[11]; JMP = in_9[12];
  //   JSP = in_9[13]; LD = in_9[14]; ST = in_9[15]; JADR = in_9[16]; TST = in_9[17]; XOR = in_9[18];
  //   STRLEN = in_9[19]; memind = in_10[0]; memdir = in_10[1]; regindpom = in_10[2]; postinc = in_10[3];
  //   preinc = in_10[4]; regdir = in_10[5]; immed = in_10[6]; EXEC = PHASEFFBUS[2]; PSWSTART = PSW[0]; PSWZ = PSW[1];
  //   PSWN = PSW[2]; PSWC = PSW[3]; PSWV = PSW[4]; PSWI = PSW[15]; rst = in_1

  // Notes on the sheet:
  //   Upravljacka jedinica
  //   Operaciona jedinica
  //   Acc
  //   contents of rom_1 (hex, n*v repeats v):
  //   400 c00 27800 0 0 28201 0 38201 27800 0 27800 0 c202 0 1c202 27a00 0 22202 0 32202 27600 0 1a202 0
  //   6202 0 0 27800 27e00 27800 0 0 1201 0 11201 27800 27100 27800 0 27800 0 27800 17800 27800 0 2d202 0
  //   3d202 13500 2d800 27800 2b900 27800 0 1b201 0 7201 80c 27800
  //   contents of rom_2 (hex, n*v repeats v):
  //   0 0 1 800 e80800 0 1680000 0 0 40 6 281000 400000 281008 400000 36 281000 400000 1c281000 400000
  //   24000000 281000 400000 295000 400000 a000 40 6 0 c000000 1c00800 280800 0 2680000 0 c000000 0
  //   c000000 66000 6 120 6 440 4000000 80 400000 10a000 400000 0 100200 4 0 c0000000 c00000 0 1500000 0 0
  //   6
endmodule

module INTR (
  input  in_1,
  input  in_2,
  input  in_3,
  input  [3:0] PHASEFFBUS,
  input  [10:0] INSTRUCBUS,
  input  [15:0] PSW,
  input  [7:0] intr,
  output [15:0] ADDIVTP,
  output [2:0] UEXT1__0,
  output inta,
  output [25:0] CMEMBUS,
  output [15:0] out_12,
  output [4:0] out_13,
  output [7:0] CFFBUS,
  output [7:0] out_15,
  output [8:0] CREGBUS,
  output rdMEM,
  output wrMEM
);

  wire and_1_out, and_2_out, and_3_out, brcnd, bruncnd, clINTR, FCBUSc, incMAR, incSP, INTc, ldMAR, ldMDR,
       ldPC, MARMX0, MARMX2, MDRMX0, MDRMX1, MDRMX2, not_2_out, not_3_out, not_4_out, not_5_out, or_2_out,
       or_3_out, PCMUX0, PCMUX1, PCMUX2, prekidc, rdMEM_t, reg8_inc_ld_1_p3, reg8_inc_ld_1_p4, reg16_ld_1_p3,
       stFETCH, wrMEM_t;
  wire [2:0] rom_1_data_2;
  wire [7:0] multiplexer_1_out;
  wire [19:18] rom_1_data;

  // REG16_LD reg16_ld_1: pin names not known; wires that end beside it: in_2, 16'hf000, reg16_ld_1_p3, in_1
  Decoder #(.select(3), .enable("false")) decoder_1 (
    .out1(bruncnd), .out2(INTc), .out3(prekidc), .out4(FCBUSc), .sel(rom_1_data_2));  // open: out0, out5, out6, out7
  // ADD16 add16_1: pin names not known; wires that end beside it: reg16_ld_1_p3, ADDIVTP, out_12
  Multiplexer #(.width(8), .enable("false")) multiplexer_1 (
    .in0({3'b000, out_15[4:0]}), .in1({8{1'b0}}), .out(multiplexer_1_out), .sel(in_1));
  // REG8_INC_LD reg8_inc_ld_1: pin names not known; wires that end beside it: in_2, multiplexer_1_out, reg8_inc_ld_1_p3, reg8_inc_ld_1_p4
  not not_1 (reg8_inc_ld_1_p4, reg8_inc_ld_1_p3);
  // REG16_LD reg16_ld_2: pin names not known; wires that end beside it: in_2, {{7{1'b0}}, intr, 1'b0}, out_12, inta
  or or_1 (reg8_inc_ld_1_p3, bruncnd, brcnd);
  ROM #(.addrWidth(5), .dataWidth(28)) rom_1 (
    .addr(out_13),
    .data({out_15[0], out_15[1], out_15[2], out_15[3], out_15[4], rom_1_data_2[0], rom_1_data_2[1], rom_1_data_2[2], rom_1_data, rdMEM_t, clINTR, stFETCH, wrMEM_t, PCMUX2, PCMUX1, PCMUX0, ldPC, MDRMX2, MDRMX1, MDRMX0, ldMDR, incSP, MARMX2, MARMX0, incMAR, ldMAR, inta}),
    .sel(1'b1));
  not not_2 (not_2_out, PHASEFFBUS[3]);
  or or_2 (or_2_out, intr[0], intr[1], intr[2], intr[3], intr[4], intr[5], intr[6], intr[7]);
  not not_3 (not_3_out, in_3);
  and and_1 (and_1_out, not_3_out, FCBUSc);
  and and_2 (and_2_out, INTc, not_2_out);
  or or_3 (or_3_out, not_4_out, not_5_out);
  not not_4 (not_4_out, or_2_out);
  not not_5 (not_5_out, PSW[15]);
  or or_4 (brcnd, and_1_out, and_2_out, and_3_out);
  and and_3 (and_3_out, prekidc, or_3_out);
  assign CMEMBUS[0] = ldMAR ? 1'b1 : 1'bz;  // Controlled_Buffer controlled_buffer_1
  assign CMEMBUS[1] = incMAR ? 1'b1 : 1'bz;  // Controlled_Buffer controlled_buffer_2
  assign CMEMBUS[2] = ldMDR ? 1'b1 : 1'bz;  // Controlled_Buffer controlled_buffer_3
  assign CMEMBUS[3] = ldPC ? 1'b1 : 1'bz;  // Controlled_Buffer controlled_buffer_4
  assign CMEMBUS[5] = MARMX0 ? 1'b1 : 1'bz;  // Controlled_Buffer controlled_buffer_5
  assign CMEMBUS[17] = MDRMX0 ? 1'b1 : 1'bz;  // Controlled_Buffer controlled_buffer_6
  assign CMEMBUS[18] = MDRMX1 ? 1'b1 : 1'bz;  // Controlled_Buffer controlled_buffer_7
  assign CMEMBUS[19] = MDRMX2 ? 1'b1 : 1'bz;  // Controlled_Buffer controlled_buffer_8
  assign CMEMBUS[20] = MARMX2 ? 1'b1 : 1'bz;  // Controlled_Buffer controlled_buffer_9
  assign CMEMBUS[21] = PCMUX0 ? 1'b1 : 1'bz;  // Controlled_Buffer controlled_buffer_10
  assign CMEMBUS[22] = PCMUX1 ? 1'b1 : 1'bz;  // Controlled_Buffer controlled_buffer_11
  assign CMEMBUS[25] = PCMUX2 ? 1'b1 : 1'bz;  // Controlled_Buffer controlled_buffer_12
  assign CREGBUS[1] = incSP ? 1'b1 : 1'bz;  // Controlled_Buffer controlled_buffer_13
  assign CFFBUS[0] = stFETCH ? 1'b1 : 1'bz;  // Controlled_Buffer controlled_buffer_14
  assign CFFBUS[7] = clINTR ? 1'b1 : 1'bz;  // Controlled_Buffer controlled_buffer_15
  assign rdMEM = rdMEM_t ? 1'b1 : 1'bz;  // Controlled_Buffer controlled_buffer_16
  assign wrMEM = wrMEM_t ? 1'b1 : 1'bz;  // Controlled_Buffer controlled_buffer_17

  assign out_15[7:5] = 3'b000;

  // Other names for the same wires on the sheet: intr7__0[7:0] = intr; ldINTREG = inta; ADDIVTP15__0[15:0] = ADDIVTP;
  //   CLK = in_2; FCBUS = in_3; INTR_t = PHASEFFBUS[3]; PSWI = PSW[15]; rst = in_1; UEXT2__0[2:0] = UEXT1__0

  // Notes on the sheet:
  //   Operaciona jedinica
  //   iVVTP
  //   Upravljacka jedinica
  //   contents of rom_1 (hex, n*v repeats v):
  //   200000 6e00000 e1 32 2104000 152 6104000 1e0 32 9104000 252 d104000 2e0 32 7104000 352 904000 1a
  //   4920040 2404 2920040 1c00 418000
  //   INTREG
endmodule

module RAM (
  input  [15:0] in_1,
  input  in_2,
  input  [7:0] in_3,
  input  in_4,
  input  in_5,
  input  in_6,
  output [7:0] out_7,
  output out_8
);

  wire and_1_out, and_2_out, CNT0, LDCNT, not_1_out, notCNT0, or_1_out, reg4_ld_sl_sr_1_p6, rsff_2_p4,
       rsff_2_p5, rsff_3_p4, sl;
  wire [3:0] CNT, LFSR;

  // RSFF rsff_1: pin names not known; wires that end beside it: 1'b0, in_2, in_6, sl
  or or_1 (or_1_out, in_4, in_5);
  // REG4_LD_SL_SR reg4_ld_sl_sr_1: pin names not known; wires that end beside it: 1'b0, 1'b0, in_2, 4'b1111, LFSR, reg4_ld_sl_sr_1_p6, sl, in_6
  // RisingEdge risingedge_1: pin names not known; wires that end beside it: or_1_out, in_2, LDCNT
  // MEM64Kx8 mem64kx8_1: pin names not known; wires that end beside it: in_1, 1'b1, in_2, in_3, out_7, in_4
  xor xor_1 (reg4_ld_sl_sr_1_p6, LFSR[2], LFSR[3]);
  and and_1 (and_1_out, CNT0, not_1_out);
  not not_1 (not_1_out, LDCNT);
  // RSFF rsff_2: pin names not known; wires that end beside it: and_1_out, in_2, LDCNT, rsff_2_p4, rsff_2_p5
  not not_2 (rsff_2_p4, in_6);
  and and_2 (and_2_out, rsff_2_p5, CNT0);
  // REG4m_DEC_LD reg4m_dec_ld_1: pin names not known; wires that end beside it: in_2, LFSR, CNT, LDCNT, notCNT0, notCNT0
  or or_2 (notCNT0, CNT[0], CNT[1], CNT[2], CNT[3]);
  // RSFF rsff_3: pin names not known; wires that end beside it: out_8, in_2, and_2_out, rsff_3_p4, out_8
  not not_3 (rsff_3_p4, in_6);
  not not_4 (CNT0, notCNT0);

  // Other names for the same wires on the sheet: ADR[15:0] = in_1; CLK = in_2; DIN[7:0] = in_3; DOUT[7:0] = out_7;
  //   fc = out_8; RDMEM = in_5; rst = in_6; WRMEM = in_4

  // Notes on the sheet:
  //   Random broj predstavlja vreme pristupa memoriji
  //   Brojac za generisanje random broja 
  //   Jedinica za generisanje function complete (fc) signala
  //   Brojac za dekrementiranje random broja
endmodule
